# Fritzing sketch P10_Receptor (saved by Fritzing 0.9.3b)
breadboards: 1

parts:
  Componente1 = Arduino Uno (Rev3)
  IR1 = TSOP312.., 314.. [package=THT]
  R1 = Resistor [tolerance=±5% resistance=220 package=THT]
  LED1 = LED - 5mm [color="Red (633nm)" package="5 mm [THT]"]

nets:
  N1: Componente1.D11_PWM/MOSI, IR1.GND
  N2: Componente1.D2, R1.Pin_1
  N3: Componente1.5V, IR1.Data
  N4: Componente1.GND, IR1.Vs, LED1.cathode
  N5: R1.Pin_0, LED1.anode
