# Fritzing sketch blink (saved by Fritzing 0.9.3b)
breadboards: 1

parts:
  Componente1 = Arduino Uno (Rev3)
  R1 = Resistor [tolerance=±5% resistance=1k package=THT]
  LED1 = LED - 5mm [color="Green (570nm)" package="5 mm [THT]"]

nets:
  N1: Componente1.D2, R1.Pin_0
  N2: Componente1.GND, LED1.anode
  N3: R1.Pin_1, LED1.cathode
