# Fritzing sketch P2_Entrada digital (saved by Fritzing 0.9.3b)
breadboards: 1

parts:
  Componente1 = Arduino Uno (Rev3)
  S1 = Pushbutton [package="[THT]"]
  R1 = Resistor [tolerance=±5% resistance=1k package=THT]
  R2 = Resistor [tolerance=±5% resistance=1k package=THT]
  LED1 = LED - 5mm [color="Red (633nm)" package="5 mm [THT]"]

nets:
  N1: Componente1.D2, R2.Pin_1
  N2: Componente1.D3_PWM, S1.Pin_1, S1.Pin_2, R1.Pin_0
  N3: Componente1.5V, S1.Pin_3, S1.Pin_4
  N4: Componente1.GND, R1.Pin_1, LED1.cathode
  N5: R2.Pin_0, LED1.anode
