# Fritzing sketch P3_Display_7_segmentos- (saved by Fritzing 0.9.3b)
breadboards: 1

parts:
  Componente1 = Arduino Uno (Rev3)
  R1 = Resistor [tolerance=±5% resistance=1k package=THT]
  R2 = Resistor [tolerance=±5% resistance=1k package=THT]
  R3 = Resistor [tolerance=±5% resistance=1k package=THT]
  R4 = Resistor [tolerance=±5% resistance=1k package=THT]
  R5 = Resistor [tolerance=±5% resistance=1k package=THT]
  R6 = Resistor [tolerance=±5% resistance=1k package=THT]
  R7 = Resistor [tolerance=±5% resistance=1k package=THT]
  DI1 = 7-Segment LED Display [package=THT]

nets:
  N1: Componente1.D8, R7.Pin_0
  N2: Componente1.D2, R1.Pin_0
  N3: Componente1.D3_PWM, R2.Pin_0
  N4: Componente1.D4, R3.Pin_0
  N5: Componente1.D5_PWM, R4.Pin_0
  N6: Componente1.D6_PWM, R5.Pin_0
  N7: Componente1.D7, R6.Pin_0
  N8: Componente1.GND, DI1.commAnode#2
  N9: R1.Pin_1, DI1.cathodeA
  N10: R2.Pin_1, DI1.cathodeB
  N11: R3.Pin_1, DI1.cathodeC
  N12: R4.Pin_1, DI1.cathodeD
  N13: R5.Pin_1, DI1.cathodeE
  N14: R6.Pin_1, DI1.cathodeF
  N15: R7.Pin_1, DI1.cathodeG
