# Fritzing sketch P6_LDR- (saved by Fritzing 0.9.3b)
breadboards: 1

parts:
  Componente1 = Arduino Uno (Rev3)
  R1 = Photocell (LDR) [package=THT]
  R2 = Rotary Potentiometer (Large) [maximum_resistance=100kΩ package=THT]
  R3 = Resistor [tolerance=±5% resistance=220 package=THT]
  LED1 = LED - 5mm [color="Red (635nm)" package="5 mm [THT]"]

nets:
  N1: Componente1.A0, R1.pin_1, R2.leg2
  N2: Componente1.D2, R3.Pin_1
  N3: Componente1.5V, R1.pin_0
  N4: Componente1.GND, R2.leg1, R2.wiper, LED1.cathode
  N5: R3.Pin_0, LED1.anode
