# Fritzing sketch RGB (saved by Fritzing 0.9.3b)
breadboards: 1

parts:
  Componente1 = Arduino Uno (Rev3)
  T1 = LM35 Temperature Sensor [package="TO92 [THT]"]
  LED1 = RGB LED (com. cathode, rgb) [package="5 mm [THT]"]
  R1 = Resistor [tolerance=±5% resistance=1k package=THT]
  R2 = Resistor [tolerance=±5% resistance=1k package=THT]
  R3 = Resistor [tolerance=±5% resistance=1k package=THT]

nets:
  N1: Componente1.A0, T1.Vout
  N2: Componente1.D2, R2.Pin_1
  N3: Componente1.D3_PWM, R3.Pin_1
  N4: Componente1.D4, R1.Pin_1
  N5: Componente1.5V, T1.+Vs
  GND: Componente1.GND, T1.GND
  N6: LED1.red_anode, R1.Pin_0
  N7: LED1.common_cathode, R3.Pin_0
  N8: LED1.green_anode, R2.Pin_0
