# Fritzing sketch Matriz_74HC595 (saved by Fritzing 0.9.3b)
breadboards: 1

parts:
  U1 = 74HC595 [package="DIP16 [THT]"]
  U2 = 74HC595 [package="DIP16 [THT]"]
  Arduino_UNO = Arduino Uno (Rev3)
  Matriz_8x8 = LBT2088AH [part_number=LBT2088AH]
  R1 = Resistor [tolerance=±5% resistance=1k package=THT]
  R2 = Resistor [tolerance=±5% resistance=1k package=THT]
  R3 = Resistor [tolerance=±5% resistance=1k package=THT]
  R4 = Resistor [tolerance=±5% resistance=1k package=THT]
  R5 = Resistor [tolerance=±5% resistance=1k package=THT]
  R6 = Resistor [tolerance=±5% resistance=1k package=THT]
  R7 = Resistor [tolerance=±5% resistance=1k package=THT]

nets:
  N1: U1.Q1, Matriz_8x8.pin_15
  N2: U1.Q2, Matriz_8x8.pin_11
  N3: U1.Q3, Matriz_8x8.pin_6
  N4: U1.Q4, Matriz_8x8.pin_10
  N5: U1.Q5, Matriz_8x8.pin_4
  N6: U1.Q6, Matriz_8x8.pin_3
  N7: U1.Q7, Matriz_8x8.pin_13
  GND: U1.GND, U2.GND, U2.OE, Arduino_UNO.GND
  VCC: U1.MR, U1.OE, U1.VCC, U2.MR, U2.VCC, Arduino_UNO.5V
  Clock_2: U1.SH_CP, Arduino_UNO.D9_PWM
  Latch_2: U1.ST_CP, Arduino_UNO.D8
  Datos_2: U1.DS, Arduino_UNO.D7
  N8: U1.Q0, Matriz_8x8.pin_16
  N9: U2.Q1, R7.Pin_0
  N10: U2.Q2, R6.Pin_0
  N11: U2.Q3, R5.Pin_0
  N12: U2.Q4, R4.Pin_0
  N13: U2.Q5, R3.Pin_0
  N14: U2.Q6, R2.Pin_0
  N15: U2.Q7, R1.Pin_0
  Clock_1: U2.SH_CP, Arduino_UNO.D12/MISO
  Latch_1: U2.ST_CP, Arduino_UNO.D11_PWM/MOSI
  Datos_1: U2.DS, Arduino_UNO.D10_PWM/SS
  N16: U2.Q0, Matriz_8x8.pin_5
  N17: Matriz_8x8.pin1, R5.Pin_1
  N18: Matriz_8x8.pin2, R7.Pin_1
  N19: Matriz_8x8.pin_7, R6.Pin_1
  N20: Matriz_8x8.pin_8, R3.Pin_1
  N21: Matriz_8x8.pin_9, R1.Pin_1
  N22: Matriz_8x8.pin_12, R4.Pin_1
  N23: Matriz_8x8.pin_14, R2.Pin_1
