# Fritzing sketch Sensor de vibracion (saved by Fritzing 0.9.3b)
breadboards: 1

parts:
  Componente1 = Arduino Uno (Rev3)
  C1 = Electrolytic Capacitor [capacitance=1µF package="100 mil [THT, electrolytic]"]
  R1 = Resistor [tolerance=±5% resistance=220 package=THT]
  LED1 = LED - 5mm [color="Red (633nm)" package="5 mm [THT]"]

nets:
  N1: Componente1.GND, C1.+, LED1.cathode
  N2: Componente1.D2, C1.-
  N3: Componente1.D3_PWM, R1.Pin_1
  N4: R1.Pin_0, LED1.anode
